# Fritzing sketch circuitFritzing (saved by Fritzing 0.9.3b)

parts:
  Raspberry_Pi_1 = Raspberry Pi 3 [part_number=RPI-3-V1.2]
  DHT1 = Humidity and Temperature Sensor DHT11

nets:
  N1: Raspberry_Pi_1.GND, DHT1.GND_1, DHT1.GND_2
  N2: Raspberry_Pi_1.GPIO23, DHT1.Data-signal
  5V: Raspberry_Pi_1.5V, DHT1.Vcc

custom parts:
  Humidity and Temperature Sensor DHT11: Digital relative humidity & temperature sensor DHT11
